// Logisim project datapath.circ as structural Verilog: 1 circuit, main circuit datapath
module datapath (
  input  [1:0] Ss,
  input  Smult,
  input  [2:0] ScompL,
  input  [2:0] ScompR,
  input  Sedg,
  input  [15:0] _185,
  input  [15:0] _16,
  input  [15:0] _1,
  input  lteq,
  input  ldH,
  input  lt,
  input  ldTh,
  input  rst,
  input  ldGxVal,
  input  ldGyVal,
  input  [15:0] _255,
  input  ldImgVal,
  input  we,
  input  [15:0] _0,
  input  Sx,
  input  Sy,
  input  [15:0] _1_2,
  input  ldX,
  input  ldY,
  input  Si,
  input  [15:0] _3,
  input  Sj,
  input  ldI,
  input  ldJ,
  input  [15:0] minus_1,
  input  Ssumxop,
  input  Ssumx,
  input  Ssumyop,
  input  Ssumy,
  input  ldSumx,
  input  ldSumy,
  input  ldMagnit,
  input  in_38
);

  wire clk_out, comparator_1_gt, comparator_1_lt, not_1_out;
  wire [15:0] adder_1_out, adder_2_out, adder_3_out, adder_4_out, adder_5_out, adder_6_out, adder_7_out,
       adder_8_out, adder_9_out, adder_10_out, adder_11_out, GxVal_q, GyVal_q, i_q, imgVal_q, j_q, magnit_q,
       multiplexer_1_out, multiplexer_2_out, multiplexer_3_out, multiplexer_4_out, multiplexer_5_out,
       multiplexer_6_out, multiplexer_7_out, multiplexer_8_out, multiplexer_9_out, multiplexer_10_out,
       multiplexer_11_out, multiplexer_12_out, multiplexer_13_out, multiplier_1_out, multiplier_2_out,
       multiplier_3_out, multiplier_4_out, multiplier_5_out, multiplier_6_out, ram_1_data, ram_2_data,
       ram_3_data, subtractor_1_out, Sumx_q, Sumy_q, Th_q, x_q, y_q;

  Clock clk (.out(clk_out));
  Multiplexer #(.width(16), .enable("false")) multiplexer_1 (
    .in0(_0), .in1(adder_5_out), .out(multiplexer_1_out), .sel(Sx));
  Multiplexer #(.width(16), .enable("false")) multiplexer_2 (
    .in0(_0), .in1(multiplexer_4_out), .out(multiplexer_2_out), .sel(Ssumx));
  RAM #(.addrWidth(16), .dataWidth(16)) ram_1 (
    .addr(adder_11_out), .data(ram_1_data), .clk(clk_out), .ld(ldGxVal), .clr(rst));  // open: sel
  RAM #(.addrWidth(16), .dataWidth(16)) ram_2 (
    .addr(adder_8_out), .data(ram_2_data), .clk(clk_out), .ld(ldImgVal), .clr(rst));  // open: sel
  Register #(.width(16)) x (.D(multiplexer_1_out), .en(ldX), .Q(x_q), .clk(clk_out), .clr(rst));
  Multiplexer #(.width(16), .enable("false")) multiplexer_3 (
    .in0(minus_1), .in1(adder_5_out), .out(multiplexer_3_out), .sel(Si));
  Register #(.width(16)) i (.D(multiplexer_3_out), .en(ldI), .Q(i_q), .clk(clk_out), .clr(rst));
  Multiplexer #(.width(16), .enable("false")) multiplexer_4 (
    .in0(multiplier_3_out), .in1(adder_2_out), .out(multiplexer_4_out), .sel(Ssumxop));
  Register #(.width(16)) Sumx (.D(multiplexer_2_out), .en(ldSumx), .Q(Sumx_q), .clk(clk_out), .clr(rst));
  Register #(.width(16)) H (.D(_16), .en(ldH), .Q(x_q), .clk(clk_out), .clr(rst));
  Register #(.width(16)) Th (.D(_185), .en(ldTh), .Q(Th_q), .clk(clk_out), .clr(rst));
  Multiplexer #(.width(16), .enable("false")) multiplexer_5 (
    .in0(_0), .in1(adder_5_out), .out(multiplexer_5_out), .sel(Sy));
  Multiplexer #(.width(16), .enable("false")) multiplexer_6 (
    .in0(minus_1), .in1(adder_5_out), .out(multiplexer_6_out), .sel(Sj));
  Multiplexer #(.width(16), .enable("false")) multiplexer_7 (
    .in0(multiplier_3_out), .in1(adder_3_out), .out(multiplexer_7_out), .sel(Ssumyop));
  Multiplexer #(.width(16), .enable("false")) multiplexer_8 (
    .in0(_0), .in1(multiplexer_7_out), .out(multiplexer_8_out), .sel(Ssumy));
  Register #(.width(16)) Sumy (.D(multiplexer_8_out), .en(ldSumy), .Q(Sumy_q), .clk(clk_out), .clr(rst));
  Register #(.width(16)) magnit (.D(adder_4_out), .en(ldMagnit), .Q(magnit_q), .clk(clk_out), .clr(rst));
  Register #(.width(16)) imgVal (.D(ram_2_data), .Q(imgVal_q), .clk(clk_out), .clr(rst));  // open: en
  Register #(.width(16)) GxVal (.D(ram_1_data), .Q(GxVal_q), .clk(clk_out), .clr(rst));  // open: en
  RAM #(.addrWidth(16), .dataWidth(16)) ram_3 (
    .addr(adder_11_out), .data(ram_3_data), .clk(clk_out), .ld(ldGyVal), .clr(rst));  // open: sel
  RAM #(.addrWidth(16), .dataWidth(16), .bus("separate")) ram_4 (
    .addr(adder_10_out), .din(multiplexer_13_out), .str(we), .clk(clk_out), .clr(rst));  // open: data, sel, ld
  Register #(.width(16)) y (.D(multiplexer_5_out), .en(ldY), .Q(y_q), .clk(clk_out), .clr(rst));
  Register #(.width(16)) j (.D(multiplexer_6_out), .en(ldJ), .Q(j_q), .clk(clk_out), .clr(rst));
  Register #(.width(16)) GyVal (.D(ram_3_data), .Q(GyVal_q), .clk(clk_out), .clr(rst));  // open: en
  Subtractor #(.width(16)) subtractor_1 (.a(x_q), .b(_1), .out(subtractor_1_out));  // open: bin, bout
  Multiplier #(.width(16)) multiplier_1 (.a(imgVal_q), .b(GxVal_q), .out(multiplier_1_out));  // open: cin, cout
  Multiplier #(.width(16)) multiplier_2 (.a(imgVal_q), .b(GyVal_q), .out(multiplier_2_out));  // open: cin, cout
  Multiplexer #(.select(2), .width(16), .enable("false")) multiplexer_9 (
    .in0(x_q), .in1(y_q), .in2(j_q), .in3(i_q), .out(multiplexer_9_out), .sel(Ss));
  Adder #(.width(16)) adder_1 (.a(y_q), .b(i_q), .out(adder_1_out));  // open: cin, cout
  Multiplexer #(.width(16), .enable("false")) multiplexer_10 (
    .in0(Sumy_q), .in1(Sumx_q), .out(multiplexer_10_out), .sel(Smult));
  Adder #(.width(16)) adder_2 (.a(Sumx_q), .b(multiplier_1_out), .out(adder_2_out));  // open: cin, cout
  Adder #(.width(16)) adder_3 (.a(multiplier_2_out), .b(Sumy_q), .out(adder_3_out));  // open: cin, cout
  Multiplier #(.width(16)) multiplier_3 (
    .a(multiplexer_10_out), .b(minus_1), .out(multiplier_3_out));  // open: cin, cout
  Adder #(.width(16)) adder_4 (.a(Sumx_q), .b(Sumy_q), .out(adder_4_out));  // open: cin, cout
  Adder #(.width(16)) adder_5 (.a(multiplexer_9_out), .b(_1_2), .out(adder_5_out));  // open: cin, cout
  Adder #(.width(16)) adder_6 (.a(x_q), .b(multiplier_4_out), .out(adder_6_out));  // open: cin, cout
  Multiplier #(.width(16)) multiplier_4 (.a(x_q), .b(adder_1_out), .out(multiplier_4_out));  // open: cin, cout
  Adder #(.width(16)) adder_7 (.a(_1_2), .b(i_q), .out(adder_7_out));  // open: cin, cout
  Multiplier #(.width(16)) multiplier_5 (.a(adder_7_out), .b(_3), .out(multiplier_5_out));  // open: cin, cout
  Multiplier #(.width(16)) multiplier_6 (.a(y_q), .b(x_q), .out(multiplier_6_out));  // open: cin, cout
  Multiplexer #(.select(3), .width(16), .enable("false")) multiplexer_11 (
    .in0(_0), .in1(_1_2), .in2(subtractor_1_out), .in3(x_q), .in4(Th_q), .out(multiplexer_11_out),
    .sel(ScompR));  // open: in5, in6, in7
  Multiplexer #(.select(3), .width(16), .enable("false")) multiplexer_12 (
    .in0(x_q), .in1(y_q), .in2(i_q), .in3(j_q), .in4(Sumx_q), .in5(Sumy_q), .in6(magnit_q),
    .out(multiplexer_12_out), .sel(ScompL));  // open: in7
  Multiplexer #(.width(16), .enable("false")) multiplexer_13 (
    .in0(_0), .in1(_255), .out(multiplexer_13_out), .sel(Sedg));
  Adder #(.width(16)) adder_8 (.a(adder_6_out), .b(i_q), .out(adder_8_out));  // open: cin, cout
  Adder #(.width(16)) adder_9 (.a(_1_2), .b(multiplier_5_out), .out(adder_9_out));  // open: cin, cout
  Adder #(.width(16)) adder_10 (.a(multiplier_6_out), .b(x_q), .out(adder_10_out));  // open: cin, cout
  not not_1 (not_1_out, comparator_1_gt);
  Comparator #(.width(16)) comparator_1 (
    .a(multiplexer_12_out), .b(multiplexer_11_out), .gt(comparator_1_gt), .lt(comparator_1_lt));  // open: eq
  Adder #(.width(16)) adder_11 (.a(adder_9_out), .b(j_q), .out(adder_11_out));  // open: cin, cout
endmodule
